# Fritzing sketch lydcone (saved by Fritzing 0.8.5b)
circuit board: 6.84856cm x 5.28697cm
breadboards: 1

parts:
  R1 = Resistor [tolerance=±5% resistance=22k package=THT]
  R2 = Resistor [tolerance=±5% resistance=22k package=THT]
  R3 = Resistor [tolerance=±5% resistance=22k package=THT]
  R4 = Resistor [tolerance=±5% resistance=22k package=THT]
  R5 = Resistor [tolerance=±5% resistance=22k package=THT]
  R6 = Resistor [tolerance=±5% resistance=10k package=THT]
  R7 = Resistor [tolerance=±5% resistance=10k package=THT]
  R8 = Resistor [tolerance=±5% resistance=10k package=THT]
  IC1 = IC, DIP package, 8 pins [chip_label="IC 741"]
  R9 = Resistor [tolerance=±5% resistance=22k package=THT]
  R10 = Resistor [tolerance=±5% resistance=22k package=THT]
  R11 = Resistor [tolerance=±5% resistance=22k package=THT]
  R12 = Resistor [tolerance=±5% resistance=22k package=THT]
  R13 = Resistor [tolerance=±5% resistance=10k package=THT]
  R14 = Resistor [tolerance=±5% resistance=22k package=THT]
  R15 = Resistor [tolerance=±5% resistance=10k package=THT]
  R16 = Resistor [tolerance=±20% resistance=10k package=THT]
  R17 = Resistor [tolerance=±5% resistance=10k package=THT]
  R18 = Resistor [tolerance=±5% resistance=22k package=THT]
  R19 = Resistor [tolerance=±5% resistance=22k package=THT]
  R20 = Resistor [tolerance=±5% resistance=22k package=THT]
  R21 = Resistor [tolerance=±5% resistance=22k package=THT]
  R22 = Resistor [tolerance=±5% resistance=10k package=THT]
  R23 = Resistor [tolerance=±5% resistance=22k package=THT]
  R24 = Resistor [tolerance=±5% resistance=10k package=THT]
  C1 = Electrolytic Capacitor [capacitance=0.22mF package="100 mil [THT, electrolytic]"]
  SPKR1 = Loudspeaker
  Part1 = Arduino Uno (Rev3)

nets:
  N1: R1.Pin_0, R2.Pin_1, R6.Pin_1
  GND: R1.Pin_1, IC1.pin4, R10.Pin_1, R23.Pin_1, SPKR1.pin1, Part1.GND
  N2: R2.Pin_0, Part1.D0/RX
  N3: R3.Pin_0, Part1.D1/TX
  N4: R3.Pin_1, R6.Pin_0, R7.Pin_1
  N5: R4.Pin_0, Part1.D2
  N6: R4.Pin_1, R7.Pin_0, R8.Pin_1
  N7: R5.Pin_0, Part1.D3_PWM
  N8: R5.Pin_1, R8.Pin_0, IC1.pin3, R9.Pin_1, R15.Pin_0, R17.Pin_0, R18.Pin_1
  N9: IC1.pin6, C1.+
  N10: R9.Pin_0, Part1.D7
  N11: R10.Pin_0, R12.Pin_1, R16.Pin_1
  N12: R11.Pin_0, Part1.D6_PWM
  N13: R11.Pin_1, R13.Pin_0, R15.Pin_1
  N14: R12.Pin_0, Part1.D4
  N15: R13.Pin_1, R14.Pin_1, R16.Pin_0
  N16: R14.Pin_0, Part1.D5_PWM
  N17: R17.Pin_1, R20.Pin_1, R22.Pin_0
  N18: R18.Pin_0, Part1.D11_PWM/MOSI
  N19: R19.Pin_0, Part1.D8
  N20: R19.Pin_1, R23.Pin_0, R24.Pin_1
  N21: R20.Pin_0, Part1.D10_PWM/SS
  N22: R21.Pin_0, Part1.D9_PWM
  N23: R21.Pin_1, R22.Pin_1, R24.Pin_0
  N24: C1.-, SPKR1.pin2
